# Fritzing sketch flight_controller (saved by Fritzing 0.9.3b)

parts:
  Часть1 = Arduino Nano (Rev3.0) (ICSP)
  Часть2 = MicroSD Card Module
  GY2 = MPU-6050 Board GY-521 [form="♀ (female)" package=THT]
  GY-NEO6MV3 = SUP500F [package=sup500f]
  Part1 = KY-012 Active Buzzer Module [package="Breakout board"]
  VCC2 = Battery block 9V
  IC2 = Voltage Regulator [package=78xxl]
  U5 = Voltage Regulator [package=sot223]
  Часть3 = Adafruit BMP180
  S1 = Pushbutton [package=THT]  # not connected
  LED1 = LED - 5mm [color="Red (633nm)" package="5 mm [THT]"]
  LoRa_Module1 = Ra-01 - LoRa Module SX1278 [part_number=SX1278]

nets:
  N1: Часть1.D1/TX, GY-NEO6MV3.VCC
  N2: Часть1.D2, LoRa_Module1.DIO0
  N3: Часть1.D4, LED1.anode
  N4: Часть1.D5, Часть2.CS
  N5: Часть1.D9, LoRa_Module1.RESET
  N6: Часть1.D10, LoRa_Module1.NSS
  N7: Часть1.D11/MOSI, Часть2.MOSI
  N8: Часть1.D12/MISO, Часть2.SCK
  N9: Часть1.VIN, IC2.OUT
  GND: Часть1.GND, Часть2.GND, Part1.-, LED1.cathode
  N10: Часть1.A5, GY2.pin3, Часть3.SCL
  N11: Часть1.A4, GY2.pin4, Часть3.SDA
  N12: Часть1.D13/SCK, Часть2.MISO
  N13: GY2.pin1, U5.IN
  N14: GY-NEO6MV3.RX-I, VCC2.-, IC2.GND

notes:
  GND: Black
  VCC: Red
  RX: Yellow
  TX: Green
  7805
  3.3V

custom parts:
  MPU-6050 Board GY-521: Acelerometro y Giroscopio MPU-6050 Board GY-521
  KY-012 Active Buzzer Module: Active Piezoelectric Buzzer Module Keyes KY-012, it produces single-tone sound when signal is high.
  Adafruit BMP180: This precision sensor from Bosch is the best low-cost sensing solution for measuring barometric pressure and temperature. Because pressure changes with altitude you can also use it as an altimeter! The sensor is soldered onto a PCB with a 3.3V regulator, I2C level shifter and pull-up resistors on the I2C pins. The BMP180 is the next-generation of sensors from Bosch, and replaces the BMP085.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
  Ra-01 - LoRa Module SX1278: The Ra-01 LoRa Module featuring the SX1278 engine by Semtech. Module by AI-Thinker. Module (Ra-01) specifications from: https://www.banggood.com/Ra-01-Smart-Electronics-SX1278-LoRa-Spread-Spectrum-Wireless-Module-Ultra-Far-10KM-433M-p-1130769.html Description: Power supply: DC1.8-3.7V(3.3V) Chip: SX1278 Frequency: 433Mhz Operating temperature: -40~+85°C On Sheild Description (may vary by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
