# Fritzing sketch flight_controller_gsm (saved by Fritzing 0.9.3b)

parts:
  Часть1 = Arduino Nano (Rev3.0) (ICSP)
  Часть2 = MicroSD Card Module
  GY2 = MPU-6050 Board GY-521 [form="♀ (female)" package=THT]
  GSM_SIM_GPSR_SMS_SIM900_SIM1 = SIM800L [package=THT]
  GY-NEO6MV3 = SUP500F [package=sup500f]
  R1 = Resistor [tolerance=±5% resistance=220 package=THT]
  R2 = Resistor [tolerance=±5% resistance=220 package="2010 [SMD]"]
  Part1 = KY-012 Active Buzzer Module [package="Breakout board"]
  VCC2 = Battery block 9V
  IC2 = Voltage Regulator [package=78xxl]
  U5 = Voltage Regulator [package=sot223]
  Часть3 = Adafruit BMP180
  S1 = Pushbutton [package=THT]  # not connected
  LED1 = LED - 5mm [color="Red (633nm)" package="5 mm [THT]"]

nets:
  N1: Часть1.D1/TX, GY-NEO6MV3.VCC
  N2: Часть1.D0/RX, R1.Pin_1
  N3: Часть1.D4, LED1.anode
  N4: Часть1.D5, Часть2.CS
  N5: Часть1.D9, GSM_SIM_GPSR_SMS_SIM900_SIM1.SIM_TXD
  N6: Часть1.D10, GSM_SIM_GPSR_SMS_SIM900_SIM1.SIM_RXD
  N7: Часть1.D11/MOSI, Часть2.MOSI
  N8: Часть1.D12/MISO, Часть2.SCK
  N9: Часть1.VIN, IC2.OUT
  GND: Часть1.GND, Часть2.GND, Part1.-, LED1.cathode
  N10: Часть1.A5, GY2.pin3, Часть3.SCL
  N11: Часть1.A4, GY2.pin4, Часть3.SDA
  N12: Часть1.D13/SCK, Часть2.MISO
  N13: GY2.pin1, U5.IN
  N14: GSM_SIM_GPSR_SMS_SIM900_SIM1.5V, GY-NEO6MV3.TX-O
  N15: GY-NEO6MV3.RX-I, R2.Pin_1, VCC2.-, IC2.GND
  N16: GY-NEO6MV3.GND, R1.Pin_0, R2.Pin_0

notes:
  GND: Black
  VCC: Red
  RX: Yellow
  TX: Green
  4.7kOhm
  10kOhm
  7805
  3.3V

custom parts:
  MPU-6050 Board GY-521: Acelerometro y Giroscopio MPU-6050 Board GY-521
  KY-012 Active Buzzer Module: Active Piezoelectric Buzzer Module Keyes KY-012, it produces single-tone sound when signal is high.
  Adafruit BMP180: This precision sensor from Bosch is the best low-cost sensing solution for measuring barometric pressure and temperature. Because pressure changes with altitude you can also use it as an altimeter! The sensor is soldered onto a PCB with a 3.3V regulator, I2C level shifter and pull-up resistors on the I2C pins. The BMP180 is the next-generation of sensors from Bosch, and replaces the BMP085.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
