# Fritzing sketch flight_controller_logger (saved by Fritzing 0.9.3b)

parts:
  Часть1 = Arduino Nano (Rev3.0) (ICSP)
  Часть2 = MicroSD Card Module
  GY2 = MPU-6050 Board GY-521 [form="♀ (female)" package=THT]
  Part1 = KY-012 Active Buzzer Module [package="Breakout board"]
  IC2 = Voltage Regulator [package=78xxl]
  Часть3 = Adafruit BMP180
  S1 = Pushbutton [package=THT]
  Part2 = KY-019 5V Relay Module [package="Breakout board"]
  L1 = Inductor [package="0805 [SMD]"]
  VCC1 = Battery  # not connected

nets:
  N1: Часть1.D5, Часть2.CS
  N2: Часть1.D6, Part1.S
  N3: Часть1.D9, Part2.S
  N4: Часть1.D11/MOSI, Часть2.MOSI
  N5: Часть1.D12/MISO, Часть2.MISO
  N6: Часть1.VIN, IC2.OUT
  GND: Часть1.GND, Часть2.GND
  N7: Часть1.A5, GY2.pin3, Часть3.SCL
  N8: Часть1.A4, GY2.pin4, Часть3.SDA
  N9: Часть1.3V3, GY2.pin1
  N10: Часть1.D13/SCK, Часть2.SCK
  N11: Part1.-, Часть3.GND, L1.pin_0
  N12: IC2.IN, S1.leg0, Part2.Common
  N13: Part2.NO, L1.pin_1

notes:
  7805
  Ignitor

custom parts:
  MPU-6050 Board GY-521: Acelerometro y Giroscopio MPU-6050 Board GY-521
  KY-012 Active Buzzer Module: Active Piezoelectric Buzzer Module Keyes KY-012, it produces single-tone sound when signal is high.
  Adafruit BMP180: This precision sensor from Bosch is the best low-cost sensing solution for measuring barometric pressure and temperature. Because pressure changes with altitude you can also use it as an altimeter! The sensor is soldered onto a PCB with a 3.3V regulator, I2C level shifter and pull-up resistors on the I2C pins. The BMP180 is the next-generation of sensors from Bosch, and replaces the BMP085.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
  KY-019 5V Relay Module: KY-019 5V Relay module, used to control AC circuits.
