# Fritzing sketch flight_controller_simple (saved by Fritzing 0.9.3b)

parts:
  Часть1 = Arduino Nano (Rev3.0) (ICSP)
  Часть2 = Adafruit BMP180
  e-radionica_com1 = LM393 LDR breakout [part_number=100027]
  e-radionica_com2 = LM393 LDR breakout [part_number=100027]
  S1 = Round Pushbutton
  Part1 = KY-017 Mercury Tilt Switch [package="Breakout board"]
  Part2 = KY-019 5V Relay Module [package="Breakout board"]
  Part3 = KY-019 5V Relay Module [package="Breakout board"]
  VCC1 = Battery block 9V
  VCC2 = Battery
  S2 = Pushbutton [package=THT]
  LED1 = LED - 5mm [color="Red (633nm)" package="5 mm [THT]"]
  L1 = Inductor [package="400 mil [THT]"]
  Part4 = KY-012 Active Buzzer Module [package="Breakout board"]

nets:
  N1: Часть1.D2, Part4.S
  N2: Часть1.D3, Part3.S
  N3: Часть1.D4, Part2.NO
  N4: Часть1.D5, LED1.anode
  N5: Часть1.D6, Part1.S
  N6: Часть1.D7, e-radionica_com1.DO
  N7: Часть1.D8, e-radionica_com2.DO
  N8: Часть1.VIN, S1.leg1
  N9: Часть1.GND, Part3.-, VCC1.-, LED1.cathode, Part4.-
  N10: Часть1.5V, Part3.+, S2.leg0
  N11: Часть1.A5, Часть2.SCL
  N12: Часть1.A4, Часть2.SDA
  N13: S1.leg0, VCC1.+
  N14: Part2.S, S2.leg1
  N15: Part3.NC, L1.pin_1
  N16: Part3.Common, VCC2.+

notes:
  Jumper
  Ignitor
  KY-017/SW-420
  LM393 (upper)
  LM393 (bottom)
  Relay (NO)
  Relay (NC)
  BMP180/BME280
  2X18650 (9V)

custom parts:
  Adafruit BMP180: This precision sensor from Bosch is the best low-cost sensing solution for measuring barometric pressure and temperature. Because pressure changes with altitude you can also use it as an altimeter! The sensor is soldered onto a PCB with a 3.3V regulator, I2C level shifter and pull-up resistors on the I2C pins. The BMP180 is the next-generation of sensors from Bosch, and replaces the BMP085.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
  KY-017 Mercury Tilt Switch: Arduino KY-017 mercury tilt switch module, it uses a small mercury ball that completes the circuit when you tilt the module.
  KY-019 5V Relay Module: KY-019 5V Relay module, used to control AC circuits.
  KY-012 Active Buzzer Module: Active Piezoelectric Buzzer Module Keyes KY-012, it produces single-tone sound when signal is high.
