# Fritzing sketch rc_reciever (saved by Fritzing 0.9.3b)

parts:
  Часть1 = Arduino Nano (Rev3.0) (ICSP)
  Часть2 = NRF24L01+ Breakout Board
  U3 = RELAY [package=relay-jzc]
  VCC2 = Battery  # not connected
  VCC1 = Battery block 9V
  S2 = Pushbutton [package=THT]  # not connected
  LED2 = LEDs [package=led10mm]
  Part1 = KY-012 Active Buzzer Module [package="Breakout board"]
  U4 = Voltage Regulator [package=sot223]
  IC1 = Voltage Regulator [package=78xxl]
  Tx2 = mystery part, 3 pins [chip_label=?]
  R1 = Resistor [tolerance=±5% resistance=220 package="0805 [SMD]"]  # not connected
  LED3 = smd LED [color="Red (633nm)" package="1206 [SMD]"]  # not connected
  L1 = Inductor [package="1206 [SMD]"]  # not connected

nets:
  N1: Часть1.D0/RX, Tx2.pin1
  N2: Часть1.D5, LED2.C
  N3: Часть1.D6, U3.MAIN
  N4: Часть1.D9, Часть2.CE
  N5: Часть1.D10, Часть2.CS
  N6: Часть1.D11/MOSI, Часть2.MOSI
  N7: Часть1.D12/MISO, Часть2.MISO
  N8: Часть1.VIN, IC1.OUT
  N9: Часть1.5V, Part1.S
  N10: Часть1.D13/SCK, Часть2.SCK
  N11: Часть2.GND, U4.ADJ
  N12: Часть2.VCC, U4.OUT
  N13: VCC1.-, IC1.GND

notes:
  Ignitor
  3.3V
  7805
  2х18650
  RF433
  1K

custom parts:
  KY-012 Active Buzzer Module: Active Piezoelectric Buzzer Module Keyes KY-012, it produces single-tone sound when signal is high.
