# Fritzing sketch control (saved by Fritzing 0.9.3b)

parts:
  Часть1 = Arduino Nano (Rev3.0) (ICSP)
  LoRa_Module2 = Ra-01 - LoRa Module SX1278 [part_number=SX1278]
  VCC2 = Battery block 9V
  Power = LEDs [package=led10mm]
  Ignitor = LEDs [package=led10mm]
  Rocket = LEDs [package=led10mm]
  Engine_start = Round Pushbutton
  Power_2 = SWITCH-SPST-2 [package=switch-spst-vertical]
  Rocket_2 = SWITCH-SPST-2 [package=switch-spst-vertical]
  IC1 = Voltage Regulator [package=78xxl]
  Ignitor_2 = SWITCH-SPST-2 [package=switch-spst-vertical]
  o1 = Module display OLED I2C 128x64 SSD1306 [package=THT]

nets:
  GND: Часть1.GND, LoRa_Module2.GND, VCC2.-, Power.C, Ignitor.C, Rocket.C, IC1.GND, o1.GND
  N1: Часть1.D2, LoRa_Module2.DIO0
  N2: Часть1.D3, Engine_start.leg1
  N3: Часть1.D4, Rocket_2.P
  N4: Часть1.D5, Ignitor_2.P
  N5: Часть1.D6, Rocket.A
  N6: Часть1.D7, Ignitor.A
  N7: Часть1.D8, Power.A
  N8: Часть1.D9, LoRa_Module2.RESET
  N9: Часть1.D10, LoRa_Module2.NSS
  N10: Часть1.D11/MOSI, LoRa_Module2.MOSI
  N11: Часть1.D12/MISO, LoRa_Module2.MISO
  N12: Часть1.VIN, Power_2.O
  5V: Часть1.5V, Engine_start.leg0, Rocket_2.O, o1.VCC
  N13: Часть1.A5, o1.SCL
  N14: Часть1.A4, o1.SDA
  3V3: Часть1.3V3, LoRa_Module2.3.3V
  N15: Часть1.D13/SCK, LoRa_Module2.SCK
  N16: Power_2.P, IC1.OUT

custom parts:
  Ra-01 - LoRa Module SX1278: The Ra-01 LoRa Module featuring the SX1278 engine by Semtech. Module by AI-Thinker. Module (Ra-01) specifications from: https://www.banggood.com/Ra-01-Smart-Electronics-SX1278-LoRa-Spread-Spectrum-Wireless-Module-Ultra-Far-10KM-433M-p-1130769.html Description: Power supply: DC1.8-3.7V(3.3V) Chip: SX1278 Frequency: 433Mhz Operating temperature: -40~+85°C On Sheild Description (may vary by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
  Module display OLED I2C 128x64 SSD1306: Ecran OLED I2C SSD163 de 128x64 avec connexion I2C
