# Fritzing sketch ignitor (saved by Fritzing 0.9.3b)

parts:
  Часть1 = Arduino Nano (Rev3.0) (ICSP)
  LoRa_Module2 = Ra-01 - LoRa Module SX1278 [part_number=SX1278]
  L1 = Inductor [package="0603 [SMD]"]
  Part1 = KY-019 5V Relay Module [package="Breakout board"]
  VCC1 = Battery
  R1 = Resistor [tolerance=±5% resistance=220 package="0805 [SMD]"]
  VCC2 = Battery block 9V
  LED1 = LEDs [package=led10mm]
  U1 = V_REG_LD1117VXX [package=78xxl]
  U2 = SWITCH-SPST-2 [package=switch-spst-vertical]

nets:
  GND: Часть1.GND, LoRa_Module2.GND, Part1.-, VCC2.-, LED1.A, U1.GND
  N1: Часть1.D2, LoRa_Module2.DIO0
  N2: Часть1.D4, Part1.S
  N3: Часть1.D5, L1.pin_1, Part1.NO
  N4: Часть1.D6, LED1.C
  N5: Часть1.D9, LoRa_Module2.RESET
  N6: Часть1.D10, LoRa_Module2.NSS
  N7: Часть1.D11/MOSI, LoRa_Module2.MOSI
  N8: Часть1.D12/MISO, LoRa_Module2.MISO
  N9: Часть1.VIN, U2.O
  N10: Часть1.5V, Part1.+
  N11: Часть1.A2, R1.Pin_0
  3V3: Часть1.3V3, LoRa_Module2.3.3V
  N12: Часть1.D13/SCK, LoRa_Module2.SCK
  N13: Part1.Common, VCC1.+
  N14: VCC2.+, U1.OUT
  N15: U1.IN, U2.P

custom parts:
  Ra-01 - LoRa Module SX1278: The Ra-01 LoRa Module featuring the SX1278 engine by Semtech. Module by AI-Thinker. Module (Ra-01) specifications from: https://www.banggood.com/Ra-01-Smart-Electronics-SX1278-LoRa-Spread-Spectrum-Wireless-Module-Ultra-Far-10KM-433M-p-1130769.html Description: Power supply: DC1.8-3.7V(3.3V) Chip: SX1278 Frequency: 433Mhz Operating temperature: -40~+85°C On Sheild Description (may vary by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
  KY-019 5V Relay Module: KY-019 5V Relay module, used to control AC circuits.
