# Fritzing sketch scale_2.0 (saved by Fritzing 0.9.3b)

parts:
  Часть1 = Arduino Uno (Rev3)  # not connected
  Часть2 = HX711 Weighing Sensor Module
  Часть4 = Memoire 1.0 - SD card log shield
  VCC3 = Battery
  IC1 = Voltage Regulator [package=78xxl]
  S2 = Pushbutton [package=THT]
  LED1 = LEDs [package=led10mm]
  LED2 = LEDs [package=led10mm]

nets:
  N1: Часть2.DO/RX, Часть4.A_IN_1
  N2: Часть2.CK/TX, Часть4.A_IN_0
  N3: Часть4.DIG_6, LED2.C
  N4: Часть4.DIG_7, LED1.C
  N5: Часть4.GND, VCC3.-
  N6: IC1.IN, S2.leg0

notes:
  7805
  4AA
