# Fritzing sketch scale_3.0 (saved by Fritzing 0.9.3b)

parts:
  Часть1 = Arduino Uno (Rev3)  # not connected
  Часть2 = HX711 Weighing Sensor Module
  Часть4 = Memoire 1.0 - SD card log shield
  VCC3 = Battery
  IC1 = Voltage Regulator [package=78xxl]
  S2 = Pushbutton [package=THT]
  LED1 = LEDs [package=led10mm]
  LED2 = LEDs [package=led10mm]
  Part1 = KY-019 5V Relay Module [package="Breakout board"]
  L1 = Inductor [package="0805 [SMD]"]
  VCC4 = Battery
  S3 = Load Sensor - 50kg [part_number=SEN-10245]
  R1 = Resistor [tolerance=±5% resistance=220 package="2512 [SMD]"]
  R2 = Resistor [tolerance=±5% resistance=220 package="2512 [SMD]"]

nets:
  N1: Часть2.DO/RX, Часть4.A_IN_1
  N2: Часть2.CK/TX, Часть4.A_IN_0
  N3: Часть2.E+, S3.R
  N4: Часть2.E-, S3.B, R2.Pin_1
  N5: Часть2.A+, S3.W, R1.Pin_1
  N6: Часть2.A-, R1.Pin_0, R2.Pin_0
  N7: Часть4.DIG_9, Part1.S
  N8: Часть4.DIG_6, LED2.C
  N9: Часть4.DIG_7, LED1.C
  N10: Часть4.GND, VCC3.-, Part1.-
  N11: Часть4.VIN, Part1.+
  N12: IC1.IN, S2.leg0
  N13: Part1.NC, L1.pin_0
  N14: Part1.Common, VCC4.+

notes:
  7805
  4AA
  1kOhm

custom parts:
  KY-019 5V Relay Module: KY-019 5V Relay module, used to control AC circuits.
  Battery: Your standard 2x 18650 battery pack (7,4 Volts)
  Load Sensor - 50kg: Half-wheatstone bridge Load Cell modified from the Fritzing Repo This load sensor, sometimes called a strain gauge, is the same one found in digital bathroom scales (you know, the ones you use in January for your New Year's resolutions, and then forget about a month later). This sensor can measure up to about 110 pounds.
