# Fritzing sketch silo_launcher (saved by Fritzing 0.9.3b)

parts:
  Часть1 = Arduino Nano (Rev3.0)
  Part1 = KY-019 5V Relay Module [package="Breakout board"]
  Part2 = KY-019 5V Relay Module [package="Breakout board"]
  J1 = Basic Servo
  Part3 = KY-012 Active Buzzer Module [package="Breakout board"]
  IC1 = Voltage Regulator [package=78xxl]
  BAT2 = 12 battery [package=battery]
  L1 = Solenoid
  S1 = Pushbutton [package=THT]
  VCC2 = Battery
  L2 = Inductor [package="1206 [SMD]"]

nets:
  GND: Часть1.GND, J1.gnd, IC1.GND, VCC2.-
  N1: Часть1.D3, Part3.S
  N2: Часть1.D5, Part2.S
  N3: Часть1.D7, Part1.S
  N4: Часть1.D10, J1.pulse
  VIN: Часть1.VIN, J1.vcc, IC1.OUT
  N5: Part1.-, L2.pin_0
  N6: Part1.Common, VCC2.+
  N7: Part1.NO, L2.pin_1
  N8: Part2.Common, BAT2.+
  N9: Part2.NO, L1.pin2
  N10: IC1.IN, S1.leg0
  N11: BAT2.-, L1.pin1

notes:
  Solenoid Valve
  Ignitor

custom parts:
  KY-019 5V Relay Module: KY-019 5V Relay module, used to control AC circuits.
  KY-012 Active Buzzer Module: Active Piezoelectric Buzzer Module Keyes KY-012, it produces single-tone sound when signal is high.
  12 battery: 12V lead acid type battery, like the Husqvarna YTH2448 12V 35AH battery. This is the mini version 1/4 the size of the actual battery to be closer to typical breadboard parts (around 2in wide rathher than 7in). The pads in pcb are sized to accomidate up to 14ga wire (as these batterys will deliver high currents.)
  Battery: Your standard 2x 18650 battery pack (7,4 Volts)
